# Fritzing sketch SchemaProjet (saved by Fritzing 0.9.4)
breadboards: 1

parts:
  Raspberry_Pi_1 = Raspberry Pi 3 [part_number=RPI-3-V1.2]
  TB6600_(hy-div268n) = tb6600 [chip_label=? package=THT]
  Stepper_Motor_NEMA_17 = Stepper Motor - Bipolar  # not connected
  Alimentation_12 = Power plug

nets:
  N1: Raspberry_Pi_1.GND, TB6600_(hy-div268n).DIR-, TB6600_(hy-div268n).PUL-
  N2: Raspberry_Pi_1.GPIO21, TB6600_(hy-div268n).ENA+
  N3: Raspberry_Pi_1.GPIO20, TB6600_(hy-div268n).DIR+
  N4: Raspberry_Pi_1.GPIO16, TB6600_(hy-div268n).PUL+
  GND: TB6600_(hy-div268n).GND, Alimentation_12.GND
  VCC: TB6600_(hy-div268n).VCC, Alimentation_12.VCC

custom parts:
  tb6600: A dummy, proxy, ersatz, stand-in part for whatever you want. With 12 pins on a 100 mil inline pin header footprint.
